# Fritzing sketch desenho (saved by Fritzing 0.9.3b)
breadboards: 2

parts:
  Part3 = Infra red receiver
  U3 = LCD-16X2 [package=lcd-16x2_noholes]
  LCM1602_IIC1 = LCM1602 IIC [part_number="LCM1602 IIC" chip_label="LCM1602 IIC" package="DIP (Dual Inline) [THT]"]
  U4 = 4-Channel 5v Relay Shield [package=relay-4ch5v10a]
  U5 = NodeMCU V1.0

nets:
  GND: Part3.GND, LCM1602_IIC1.GND, U4.GND, U5.GND
  VCC: Part3.VCC, LCM1602_IIC1.VCC, U4.VCC, U5.3V3
  VSS: U3.VSS, LCM1602_IIC1.VSS
  VDD: U3.VDD, LCM1602_IIC1.VDD
  N1: U3.VO, LCM1602_IIC1.V0
  N2: U3.RS, LCM1602_IIC1.RS
  N3: U3.R_W, LCM1602_IIC1.RW
  N4: U3.E, LCM1602_IIC1.E
  N5: U3.DB0, LCM1602_IIC1.D0
  N6: U3.DB1, LCM1602_IIC1.D1
  N7: U3.DB2, LCM1602_IIC1.D2
  N8: U3.DB3, LCM1602_IIC1.D3
  N9: U3.DB4, LCM1602_IIC1.D4
  N10: U3.DB5, LCM1602_IIC1.D5
  N11: U3.DB6, LCM1602_IIC1.D6
  N12: U3.DB7, LCM1602_IIC1.D7
  N13: U3.A, LCM1602_IIC1.A
  N14: U3.K, LCM1602_IIC1.K
  N15: LCM1602_IIC1.SDA, U5.D1
  N16: LCM1602_IIC1.SCL, U5.D2
  N17: U4.IN1, U5.D0
  N18: U4.K2-On, U4.K4-Off

notes:
  interruptor
  Lâmpada

custom parts:
  LCM1602 IIC: I2C-Module to use a 1602 or 2004 LCD on with the wire.h libory Serial LCD Modul
  4-Channel 5v Relay Shield: 4 Channel 5v Relay Shield w. 2x SPD-06VDC-SD-C
  NodeMCU V1.0: ESP8266 based NodeMCU
